# Fritzing sketch schema-ssl-(fritzing) (saved by Fritzing 0.8.7b)
circuit board: 8.46667cm x 5.64444cm
breadboards: 1

parts:
  R1 = PHOTOCELL [package=photocell-kit]
  LED4 = LED - 5mm [color="White (8000K)" package="5 mm [THT]"]
  LED5 = LED - 5mm [color="Red (633nm)" package="5 mm [THT]"]
  LED6 = LED - 5mm [color="Green (570nm)" package="5 mm [THT]"]
  J1 = Piezo Speaker
  Componente1 = Arduino Uno (Rev3)
  R6 = Resistor [tolerance=±5% resistance=220 package=THT]
  R7 = Resistor [tolerance=±5% resistance=220 package=THT]
  R8 = Resistor [tolerance=±5% resistance=220 package=THT]
  R12 = Resistor [tolerance=±5% resistance=220 package=THT]
  R13 = Resistor [tolerance=±5% resistance=220 package=THT]
  VCC1 = Battery block 9V  # not connected

nets:
  N1: R1.P$1, Componente1.A0, R12.Pin_1
  N2: R1.P$2, LED4.cathode, LED5.cathode, LED6.cathode, J1.pin1, Componente1.GND
  N3: LED4.anode, R13.Pin_1
  N4: LED5.anode, R7.Pin_1
  N5: LED6.anode, R6.Pin_1
  N6: J1.pin2, Componente1.D13/SCK
  N7: Componente1.D3_PWM, R6.Pin_0
  N8: Componente1.D4, R7.Pin_0
  N9: Componente1.D5_PWM, R13.Pin_0
  N10: Componente1.5V, R8.Pin_0, R12.Pin_0
